# Fritzing sketch WetterstationDaidalos (saved by Fritzing 0.9.1b)

parts:
  U1 = 74HC04_HEX_INVERTER [part_number=CD40106BE package=dil14]
  C1 = Ceramic Capacitor [capacitance=100nF package="100 mil [THT, multilayer]"]
  R1 = Resistor [tolerance=±5% resistance=4.7k package=THT]
  D1 = Rectifier Diode [part_number=1N4148 package="300 mil [THT]"]
  R2 = Resistor [tolerance=±5% resistance=100k package=THT]
  S1 = Reed switch [part_number=Rain package=THT]
  R3 = Resistor [tolerance=±5% resistance=4.7k package=THT]
  D2 = Rectifier Diode [part_number=1N4148 package="300 mil [THT]"]
  Part2 = Arduino Prototyping Shield
  R4 = Resistor [tolerance=±5% resistance=100k package=THT]
  S2 = Reed switch [part_number="Wind speed" package=THT]
  C2 = Ceramic Capacitor [capacitance=100nF package="100 mil [THT, multilayer]"]
  R9 = Trimmer Potentiometer [maximum_resistance=0.1MΩ part_number="Wind direction" package=THT]
  R5 = Resistor [tolerance=±5% resistance=10k package=THT]
  R6 = Resistor [tolerance=±5% resistance=150 package=THT]
  P1 = S1133 Si Photodiode [part_number=Solar package="8mm Ceramic [THT]"]
  U2 = TMP36 [part_number="Temperature (Maxim DS18B20)" package=to-92-kit]
  U3 = TMP36 [part_number="Humidity (Honeywell HIH-5031)" package=to-92-kit]
  R7 = Resistor [tolerance=±5% resistance=4.7k package=THT]
  R8 = Resistor [tolerance=±5% resistance=100k package=THT]
  U4 = MPL3115A2 [part_number=MPL3115A2 package=lga8]

nets:
  N1: U1.1A, R3.Pin_1, D2.cathode, Part2.N$48, C2.0
  N2: U1.1Y, Part2.D2, Part2.N$61, Part2.N$62
  N3: U1.2A, Part2.N$72
  N4: U1.2Y, Part2.N$86
  N5: U1.3A, C1.1, R1.Pin_1, D1.cathode, Part2.N$77
  N6: U1.3Y, Part2.D3, Part2.N$76
  GND: U1.GND, C1.0, S1.pin_2, Part2.GND, Part2.N$71, Part2.N$118, Part2.N$313, S2.pin_2, C2.1, R9.wiper, R6.Pin_1, U2.GND, U3.GND, R8.Pin_1, U4.GND
  N7: U1.4Y, Part2.N$178
  N8: U1.4A, Part2.N$67
  N9: U1.5Y, Part2.N$87
  N10: U1.5A, Part2.N$84
  N11: U1.6Y, Part2.N$79
  N12: U1.6A, Part2.N$65
  VCC: U1.VCC, R2.Pin_1, Part2.+5V, Part2.N$55, Part2.N$232, Part2.N$307, Part2.N$315, Part2.N$362, R4.Pin_1, R5.Pin_1, P1.anode, U2.VCC, U3.VCC, R7.Pin_1
  N13: R1.Pin_0, D1.anode, R2.Pin_0, S1.pin_1, Part2.N$259, Part2.N$314
  N14: R3.Pin_0, D2.anode, Part2.N$289, R4.Pin_0, S2.pin_1
  N15: Part2.A2, Part2.N$366, R9.leg1, R5.Pin_0
  N16: Part2.D7, Part2.N$153, U2.VOUT, R7.Pin_0
  3.3V: Part2.3.3V, U4.VDD
  N17: Part2.SDA, U4.SDA
  N18: Part2.SCL, U4.SCL
  N19: Part2.A3, Part2.N$38, R6.Pin_0, P1.cathode
  N20: Part2.A4, Part2.N$408, U3.VOUT, R8.Pin_0
